// Logisim project proiect_bun.circ as structural Verilog
module main (
  input  in_1,
  input  in_2,
  input  in_3,
  output [3:0] out_4,
  output [3:0] out_5,
  output [3:0] out_6,
  output [3:0] out_7,
  output [3:0] out_8,
  output [3:0] out_9,
  output [3:0] out_10,
  output [1:0] out_11,
  output out_12,
  output [3:0] out_13,
  output out_14,
  output [3:0] out_15,
  output [3:0] out_16
);

  wire button_1_out, button_2_out, clock_1_out, debouncer_1_btndb, debouncer_2_btndb, debouncer_3_btndb,
       dmux1_2_1bit_1_dout0, dmux1_2_1bit_1_dout1, dmux1_4_1bit_1_dout1, dmux1_4_1bit_1_dout2,
       dmux1_4_1bit_1_dout3, dmux1_4_1bit_2_dout1, dmux1_4_1bit_2_dout2, dmux1_4_1bit_2_dout3, or_1_out,
       or_2_out, uc_1_alege_registrii, uc_1_introdu_caractere, uc_1_liber_ocupat, uc_1_reset_reg1,
       uc_1_reset_reg2;
  wire [3:0] dmux1_4_1_dout1, dmux1_4_1_dout2, dmux1_4_1_dout3, dmux1_4_2_dout1, dmux1_4_2_dout2,
       dmux1_4_2_dout3, mux2_1_1_dout, mux2_1_2_dout, mux2_1_3_dout, numarator_btn_up_down_1_dout;
  wire [6:0] bcddecod_1_decod, bcddecod_2_decod, bcddecod_3_decod;

  Button button_1 (.out(button_1_out));
  debouncer debouncer_1 (.btn(in_1), .R(in_2), .CLK(clock_1_out), .btndb(debouncer_1_btndb));
  Button button_2 (.out(button_2_out));
  debouncer debouncer_2 (.btn(button_1_out), .R(in_2), .CLK(clock_1_out), .btndb(debouncer_2_btndb));
  debouncer debouncer_3 (.btn(button_2_out), .R(in_2), .CLK(clock_1_out), .btndb(debouncer_3_btndb));
  Clock clock_1 (.out(clock_1_out));
  numarator_btn_up_down numarator_btn_up_down_1 (
    .btn_up(debouncer_3_btndb), .btn_down(debouncer_2_btndb), .reset(in_3),
    .dout(numarator_btn_up_down_1_dout));
  UC uc_1 (
    .adauga_cifru(debouncer_1_btndb), .reset(in_2), .clk(clock_1_out), .reg1_1(out_5), .reg1_2(out_6),
    .reg1_3(out_10), .reg2_1(out_13), .reg2_2(out_15), .reg2_3(out_16), .liber_ocupat(uc_1_liber_ocupat),
    .introdu_caractere(uc_1_introdu_caractere), .alege_registrii(uc_1_alege_registrii),
    .reset_reg2(uc_1_reset_reg2), .reset_reg1(uc_1_reset_reg1));
  LED led_1 (.in(uc_1_reset_reg2));
  or or_1 (or_1_out, in_2, uc_1_reset_reg1);
  LED led_2 (.in(uc_1_liber_ocupat));
  LED led_3 (.in(uc_1_introdu_caractere));
  LED led_4 (.in(uc_1_alege_registrii));
  or or_2 (or_2_out, in_2, uc_1_reset_reg2);
  dmux1_2 dmux1_2_1 (.din(numarator_btn_up_down_1_dout), .sel(uc_1_liber_ocupat), .dout0(out_7), .dout1(out_8));
  numaratormodulo numaratormodulo_1 (.clock(debouncer_1_btndb), .reset(in_2), .count(out_11));
  dmux1_2_1bit dmux1_2_1bit_1 (
    .din(1'b1), .sel(uc_1_alege_registrii), .dout0(dmux1_2_1bit_1_dout0), .dout1(dmux1_2_1bit_1_dout1));
  dmux1_4 dmux1_4_1 (
    .din(out_7), .sel(out_11), .dout0(out_4), .dout1(dmux1_4_1_dout1), .dout2(dmux1_4_1_dout2),
    .dout3(dmux1_4_1_dout3));
  dmux1_4 dmux1_4_2 (
    .din(out_8), .sel(out_11), .dout0(out_9), .dout1(dmux1_4_2_dout1), .dout2(dmux1_4_2_dout2),
    .dout3(dmux1_4_2_dout3));
  dmux1_4_1bit dmux1_4_1bit_1 (
    .din(dmux1_2_1bit_1_dout0), .sel(out_11), .dout0(out_12), .dout1(dmux1_4_1bit_1_dout1),
    .dout2(dmux1_4_1bit_1_dout2), .dout3(dmux1_4_1bit_1_dout3));
  dmux1_4_1bit dmux1_4_1bit_2 (
    .din(dmux1_2_1bit_1_dout1), .sel(out_11), .dout0(out_14), .dout1(dmux1_4_1bit_2_dout1),
    .dout2(dmux1_4_1bit_2_dout2), .dout3(dmux1_4_1bit_2_dout3));
  reg_4 reg_4_1 (.CLK(clock_1_out), .R(or_1_out), .L(dmux1_4_1bit_1_dout1), .d_in(dmux1_4_1_dout1), .d_out(out_5));
  reg_4 reg_4_2 (.CLK(clock_1_out), .R(or_1_out), .L(dmux1_4_1bit_1_dout2), .d_in(dmux1_4_1_dout2), .d_out(out_6));
  reg_4 reg_4_3 (.CLK(clock_1_out), .R(or_1_out), .L(dmux1_4_1bit_1_dout3), .d_in(dmux1_4_1_dout3), .d_out(out_10));
  reg_4 reg_4_4 (.CLK(clock_1_out), .R(or_2_out), .L(dmux1_4_1bit_2_dout1), .d_in(dmux1_4_2_dout1), .d_out(out_13));
  reg_4 reg_4_5 (.CLK(clock_1_out), .R(or_2_out), .L(dmux1_4_1bit_2_dout2), .d_in(dmux1_4_2_dout2), .d_out(out_15));
  reg_4 reg_4_6 (.CLK(clock_1_out), .R(or_2_out), .L(dmux1_4_1bit_2_dout3), .d_in(dmux1_4_2_dout3), .d_out(out_16));
  mux2_1 mux2_1_1 (.din0(out_5), .din1(out_13), .sel(uc_1_liber_ocupat), .dout(mux2_1_1_dout));
  mux2_1 mux2_1_2 (.din0(out_6), .din1(out_15), .sel(uc_1_liber_ocupat), .dout(mux2_1_2_dout));
  mux2_1 mux2_1_3 (.din0(out_10), .din1(out_16), .sel(uc_1_liber_ocupat), .dout(mux2_1_3_dout));
  BCDdecod bcddecod_1 (.hexa(mux2_1_1_dout), .decod(bcddecod_1_decod));
  BCDdecod bcddecod_2 (.hexa(mux2_1_2_dout), .decod(bcddecod_2_decod));
  _7_Segment_Display #(.active("false"), .decimalPoint("false")) u_7_segment_display_1 (
    .g(bcddecod_1_decod[0]), .f(bcddecod_1_decod[1]), .a(bcddecod_1_decod[6]), .b(bcddecod_1_decod[5]),
    .e(bcddecod_1_decod[2]), .d(bcddecod_1_decod[3]), .c(bcddecod_1_decod[4]));
  _7_Segment_Display #(.active("false"), .decimalPoint("false")) u_7_segment_display_2 (
    .g(bcddecod_2_decod[0]), .f(bcddecod_2_decod[1]), .a(bcddecod_2_decod[6]), .b(bcddecod_2_decod[5]),
    .e(bcddecod_2_decod[2]), .d(bcddecod_2_decod[3]), .c(bcddecod_2_decod[4]));
  BCDdecod bcddecod_3 (.hexa(mux2_1_3_dout), .decod(bcddecod_3_decod));
  _7_Segment_Display #(.active("false"), .decimalPoint("false")) u_7_segment_display_3 (
    .g(bcddecod_3_decod[0]), .f(bcddecod_3_decod[1]), .a(bcddecod_3_decod[6]), .b(bcddecod_3_decod[5]),
    .e(bcddecod_3_decod[2]), .d(bcddecod_3_decod[3]), .c(bcddecod_3_decod[4]));
endmodule

module placuta (
  input  Input_1,
  input  Input_3,
  input  Input_4,
  input  Input_5,
  input  Input_2,
  input  Input_6,
  output Output_3,
  output [3:0] Output_bus_1,
  output [3:0] Output_bus_2,
  output Output_4,
  output [3:0] Output_bus_3,
  output [3:0] Output_bus_4,
  output [3:0] Output_bus_5,
  output [3:0] Output_bus_6,
  output [3:0] Output_bus_7,
  output [1:0] Output_bus_8,
  output [2:0] Output_bus_9,
  output [6:0] Output_bus_10,
  output Output_1,
  output Output_5,
  output [3:0] Output_bus_11,
  output Output_2,
  output [3:0] Output_bus_12,
  output [3:0] Output_bus_13,
  output Output_6
);

  wire debouncer_1_btndb, debouncer_2_btndb, debouncer_3_btndb, dmux1_2_1bit_1_dout0, dmux1_2_1bit_1_dout1,
       dmux1_4_1bit_1_dout1, dmux1_4_1bit_1_dout2, dmux1_4_1bit_1_dout3, dmux1_4_1bit_2_dout1,
       dmux1_4_1bit_2_dout2, dmux1_4_1bit_2_dout3, sau_1_c, sau_2_c, uc_1_reset_reg1;
  wire [3:0] dmux1_4_1_dout1, dmux1_4_1_dout2, dmux1_4_1_dout3, dmux1_4_2_dout1, dmux1_4_2_dout2,
       dmux1_4_2_dout3, mux2_1_1_dout, mux2_1_2_dout, mux2_1_3_dout, numarator_btn_up_down_1_dout;

  debouncer debouncer_1 (.btn(Input_3), .R(Input_1), .CLK(Input_4), .btndb(debouncer_1_btndb));
  debouncer debouncer_3 (.btn(Input_6), .R(Input_1), .CLK(Input_4), .btndb(debouncer_3_btndb));
  debouncer debouncer_2 (.btn(Input_5), .R(Input_1), .CLK(Input_4), .btndb(debouncer_2_btndb));
  numarator_btn_up_down numarator_btn_up_down_1 (
    .btn_up(debouncer_2_btndb), .btn_down(debouncer_3_btndb), .reset(Input_2),
    .dout(numarator_btn_up_down_1_dout));
  UC uc_1 (
    .adauga_cifru(debouncer_1_btndb), .reset(Input_1), .clk(Input_4), .reg1_1(Output_bus_2),
    .reg1_2(Output_bus_3), .reg1_3(Output_bus_7), .reg2_1(Output_bus_11), .reg2_2(Output_bus_12),
    .reg2_3(Output_bus_13), .liber_ocupat(Output_3), .introdu_caractere(Output_4),
    .alege_registrii(Output_5), .reset_reg2(Output_6), .reset_reg1(uc_1_reset_reg1));
  sau sau_1 (.A(Input_1), .B(uc_1_reset_reg1), .C(sau_1_c));
  dmux1_2 dmux1_2_1 (.din(numarator_btn_up_down_1_dout), .sel(Output_3), .dout0(Output_bus_4), .dout1(Output_bus_5));
  numaratormodulo numaratormodulo_1 (.clock(debouncer_1_btndb), .reset(Input_1), .count(Output_bus_8));
  dmux1_2_1bit dmux1_2_1bit_1 (.din(1'b1), .sel(Output_5), .dout0(dmux1_2_1bit_1_dout0), .dout1(dmux1_2_1bit_1_dout1));
  sau sau_2 (.A(Input_1), .B(Output_6), .C(sau_2_c));
  dmux1_4 dmux1_4_1 (
    .din(Output_bus_4), .sel(Output_bus_8), .dout0(Output_bus_1), .dout1(dmux1_4_1_dout1),
    .dout2(dmux1_4_1_dout2), .dout3(dmux1_4_1_dout3));
  dmux1_4 dmux1_4_2 (
    .din(Output_bus_5), .sel(Output_bus_8), .dout0(Output_bus_6), .dout1(dmux1_4_2_dout1),
    .dout2(dmux1_4_2_dout2), .dout3(dmux1_4_2_dout3));
  dmux1_4_1bit dmux1_4_1bit_1 (
    .din(dmux1_2_1bit_1_dout0), .sel(Output_bus_8), .dout0(Output_1), .dout1(dmux1_4_1bit_1_dout1),
    .dout2(dmux1_4_1bit_1_dout2), .dout3(dmux1_4_1bit_1_dout3));
  dmux1_4_1bit dmux1_4_1bit_2 (
    .din(dmux1_2_1bit_1_dout1), .sel(Output_bus_8), .dout0(Output_2), .dout1(dmux1_4_1bit_2_dout1),
    .dout2(dmux1_4_1bit_2_dout2), .dout3(dmux1_4_1bit_2_dout3));
  reg_4 reg_4_1 (.CLK(Input_4), .R(sau_1_c), .L(dmux1_4_1bit_1_dout1), .d_in(dmux1_4_1_dout1), .d_out(Output_bus_2));
  reg_4 reg_4_2 (.CLK(Input_4), .R(sau_1_c), .L(dmux1_4_1bit_1_dout2), .d_in(dmux1_4_1_dout2), .d_out(Output_bus_3));
  reg_4 reg_4_3 (.CLK(Input_4), .R(sau_1_c), .L(dmux1_4_1bit_1_dout3), .d_in(dmux1_4_1_dout3), .d_out(Output_bus_7));
  reg_4 reg_4_4 (.CLK(Input_4), .R(sau_2_c), .L(dmux1_4_1bit_2_dout1), .d_in(dmux1_4_2_dout1), .d_out(Output_bus_11));
  reg_4 reg_4_5 (.CLK(Input_4), .R(sau_2_c), .L(dmux1_4_1bit_2_dout2), .d_in(dmux1_4_2_dout2), .d_out(Output_bus_12));
  reg_4 reg_4_6 (.CLK(Input_4), .R(sau_2_c), .L(dmux1_4_1bit_2_dout3), .d_in(dmux1_4_2_dout3), .d_out(Output_bus_13));
  mux2_1 mux2_1_1 (.din0(Output_bus_2), .din1(Output_bus_11), .sel(Output_3), .dout(mux2_1_1_dout));
  mux2_1 mux2_1_2 (.din0(Output_bus_3), .din1(Output_bus_12), .sel(Output_3), .dout(mux2_1_2_dout));
  mux2_1 mux2_1_3 (.din0(Output_bus_7), .din1(Output_bus_13), .sel(Output_3), .dout(mux2_1_3_dout));
  Controler_7segm controler_7segm_1 (
    .clk(Input_4), .S0(mux2_1_1_dout), .S1(mux2_1_2_dout), .S2(mux2_1_3_dout), .anod(Output_bus_9),
    .catod(Output_bus_10));
endmodule

// VHDL entity BCDdecod, as the project stores it:
LIBRARY ieee;
USE ieee.std_logic_1164.all;

ENTITY BCDdecod IS
  PORT (
	hexa:in std_logic_vector(3 downto 0);
	decod:out std_logic_vector(6 downto 0)
	  );
END BCDdecod;


ARCHITECTURE arch OF BCDdecod IS

BEGIN

decod<="0000001" when hexa=x"0" else
	    "1001111" when hexa=x"1" else
	    "0010010" when hexa=x"2" else
	    "0000110" when hexa=x"3" else
	    "1001100"when hexa=x"4" else
	    "0100100"when hexa=x"5" else
	    "0100000"when hexa=x"6" else
	    "0001111"when hexa=x"7" else
	    "0000000"when hexa=x"8" else
	    "0000100"when hexa=x"9" else
	    "0001000" when hexa=x"a" else
	    "1100000" when hexa=x"b" else
	    "0110001" when hexa=x"c" else
	    "1000010" when hexa=x"d" else
	    "0110000" when hexa=x"e" else
	    "0111000" when hexa=x"f" else
	    "1111111";

END arch;

// VHDL entity UC, as the project stores it:
LIBRARY ieee;
USE ieee.std_logic_1164.all;

ENTITY UC IS
  PORT (
  adauga_cifru, reset,clk: in std_logic;
 
  reg1_1,reg1_2,reg1_3,reg2_1,reg2_2,reg2_3: in std_logic_vector (3 downto 0);
  
  liber_ocupat, introdu_caractere,alege_registrii,reset_reg2,reset_reg1: out std_logic
   
    );
END UC;


ARCHITECTURE arch OF UC IS
type Stare_T is (S0,S1,S2,S3,S4,S5,S6,S7,S8);
signal stare, nxtstare:Stare_T:=S0;
begin
	process(clk,reset)
	begin
		If reset='1' then stare<=S0;
		else
			if rising_edge(clk) then
				stare<=nxtstare;
			end if;
		end if;
	
	end process;

	process(stare, adauga_cifru,reg1_1,reg1_2,reg1_3,reg2_1,reg2_2,reg2_3)
	begin
	liber_ocupat<='0';introdu_caractere<='0';alege_registrii<='0';reset_reg2<='0';reset_reg1<='0';
	case stare is
	--when S0=> liber_ocupat<='0';
	--		if adauga_cifru='1' then 
	--		nxtstare<=S1;
	--		else nxtstare<=S0;
			--introdu_caractere<='1';
			--nxtstare<=S1;
			--else nxtstare<=S0;
	--		end if;
		
	when S0=> reset_reg1<='1';reset_reg2<='1';introdu_caractere<='0';alege_registrii<='0'; if adauga_cifru='1' then nxtstare<=S1; 
			else nxtstare<=S0;
			end if;
	when S1=> reset_reg2<='0';alege_registrii<='0';introdu_caractere<='1'; if adauga_cifru='1' then nxtstare<=S2; 
			else nxtstare<=S1;
			end if;
	when S2=> reset_reg2<='0';alege_registrii<='0';introdu_caractere<='1'; if adauga_cifru='1' then nxtstare<=S3; 
			else nxtstare<=S2;
			end if;
	when S3=> reset_reg2<='0';alege_registrii<='0';introdu_caractere<='1';if adauga_cifru='1' then 
			nxtstare<=S4; liber_ocupat<='1';
			else nxtstare<=S3;
			end if;
	when S4=> reset_reg2<='0';alege_registrii<='0';alege_registrii<='1';liber_ocupat<='1'; introdu_caractere<='0';
			if adauga_cifru='1' then nxtstare<=S4;
			else nxtstare<=S5;
			end if;
					
	when S5=> reset_reg2<='0';alege_registrii<='1';liber_ocupat<='1';if adauga_cifru='1' then nxtstare<=S6; introdu_caractere<='1';
			else nxtstare<=S5;
			end if;
	when S6=> reset_reg2<='0';alege_registrii<='1';liber_ocupat<='1';introdu_caractere<='1';if adauga_cifru='1' then nxtstare<=S7;
			else nxtstare<=S6;
			end if;
	when S7=> reset_reg2<='0';alege_registrii<='1';liber_ocupat<='1';introdu_caractere<='1';if adauga_cifru='1' then nxtstare<=S8;
			else nxtstare<=S7;
			end if;
	--when S8=> reset_reg2<='0';alege_registrii<='1';liber_ocupat<='1';introdu_caractere<='1';if adauga_cifru='1' then nxtstare<=S9;
	--		else nxtstare<=S8;
	--		end if;
	when S8=> reset_reg2<='0';alege_registrii<='1';liber_ocupat<='1';introdu_caractere<='1';if adauga_cifru='1' then 
				if reg1_1=reg2_1 then
				if reg1_2=reg2_2 then
				if reg1_3=reg2_3 then
				introdu_caractere<='0';
				nxtstare<=S0; 
				else
				reset_reg2<='1';
				nxtstare<=S4;
				end if;
				end if;
				end if;
				else
				nxtstare<=S8;
				end if;
end case;
end process;


END arch;

// VHDL entity dmux1_2, as the project stores it:
LIBRARY ieee;
USE ieee.std_logic_1164.all;

ENTITY dmux1_2 IS
  PORT (
	din: in std_logic_vector (3 downto 0);
	sel:in std_logic;
	dout0,dout1: out std_logic_vector(3 downto 0)
    );
END dmux1_2;



ARCHITECTURE arch OF dmux1_2 IS

BEGIN

dout0<=din when sel='0' else "0000";

dout1<=din when sel='1' else "0000";

END arch;

// VHDL entity dmux1_4, as the project stores it:
LIBRARY ieee;
USE ieee.std_logic_1164.all;

ENTITY dmux1_4 IS
  PORT (
	din: in std_logic_vector(3 downto 0);
	sel:in std_logic_vector (1 downto 0);
	dout0,dout1,dout2,dout3: out std_logic_vector(3 downto 0)
    );
END dmux1_4;



ARCHITECTURE arch OF dmux1_4 IS

BEGIN

dout0<=din when sel="00" else "0000";

dout1<=din when sel="01" else "0000";

dout2<=din when sel="10" else "0000";

dout3<=din when sel="11" else "0000";



END arch;

// VHDL entity numaratormodulo, as the project stores it:
LIBRARY ieee;
USE ieee.std_logic_1164.all;
use ieee.std_logic_UNSIGNED.all;
 
ENTITY numaratormodulo IS
  PORT (
  		
		clock,reset:in std_logic;
		count:out std_logic_vector(1 downto 0)
    );
END numaratormodulo;
 
 
ARCHITECTURE arch OF numaratormodulo IS
 
BEGIN
 
process(clock)
variable tmp: std_logic_vector(1 downto 0):="00";
begin
if(reset='1') then
tmp:="00";
else
	if(rising_edge(clock))then
			
			if(tmp="11")then
				tmp:="00";
			else
				tmp:=tmp+1;
		end if;
	end if;
	end if;
count<=tmp;
end process;
END arch;

// VHDL entity reg_4, as the project stores it:
LIBRARY ieee;
USE ieee.std_logic_1164.all;

ENTITY reg_4 IS
  PORT (
	CLK,R,L:in std_logic;
	d_in:in std_logic_vector(3 downto 0);
	d_out:out std_logic_vector(3 downto 0)
    );
END reg_4;

ARCHITECTURE arch OF reg_4 IS
signal tmp:std_logic_vector(3 downto 0);
BEGIN
process(CLK)
begin
if(rising_edge(CLK)) then
if(R='1') then
tmp<="0000";
elsif(L='1') then 
tmp<=d_in;

else
tmp<=tmp;
end if;
end if;

end process;
d_out<=tmp;

END arch;

// VHDL entity mux2_1, as the project stores it:
LIBRARY ieee;
USE ieee.std_logic_1164.all;

ENTITY mux2_1 IS
  PORT (
din0,din1: in std_logic_vector(3 downto 0);
sel: in std_logic;
dout:out std_logic_vector(3 downto 0)
    );
END mux2_1;

ARCHITECTURE arch OF mux2_1 IS

BEGIN

with sel select dout<=din0 when '0',
				  din1 when '1',
				 
				  "0000" when others;

END arch;

// VHDL entity dmux1_4_1bit, as the project stores it:
LIBRARY ieee;
USE ieee.std_logic_1164.all;

ENTITY dmux1_4_1bit IS
  PORT (
	din: in std_logic;
	sel:in std_logic_vector (1 downto 0);
	dout0,dout1,dout2,dout3: out std_logic
    );
END dmux1_4_1bit;



ARCHITECTURE arch OF dmux1_4_1bit IS

BEGIN

dout0<=din when sel="00" else '0';

dout1<=din when sel="01" else '0';

dout2<=din when sel="10" else '0';

dout3<=din when sel="11" else '0';



END arch;

// VHDL entity dmux1_2_1bit, as the project stores it:
LIBRARY ieee;
USE ieee.std_logic_1164.all;

ENTITY dmux1_2_1bit IS
  PORT (
	din: in std_logic;
	sel:in std_logic;
	dout0,dout1: out std_logic
    );
END dmux1_2_1bit;



ARCHITECTURE arch OF dmux1_2_1bit IS

BEGIN

dout0<=din when sel='0' else '0';

dout1<=din when sel='1' else '0';

END arch;

// VHDL entity numarator_btn_up_down, as the project stores it:
LIBRARY ieee;
USE ieee.std_logic_1164.all;
use ieee.std_logic_UNSIGNED.all;
ENTITY numarator_btn_up_down IS
  PORT (
btn_up,btn_down,reset:in std_logic;
dout:out std_logic_vector(3 downto 0)
    );
END numarator_btn_up_down;


ARCHITECTURE arch OF numarator_btn_up_down IS

BEGIN
process(btn_up,btn_down)
variable tmp:std_logic_vector(3 downto 0):="0000";
begin 
if(reset='1') then
tmp:="0000";
elsif(rising_edge(btn_up)) then
if(tmp="1111") then
tmp:="0000";
else
tmp:=tmp+1;
end if;
elsif (rising_edge(btn_down)) then
if(tmp="0000") then
tmp:="1111";
else
tmp:=tmp-1;

end if;
end if;

dout<=tmp;
end process;

END arch;

// VHDL entity Controler_7segm, as the project stores it:
LIBRARY ieee;
USE ieee.std_logic_1164.all;

USE ieee.std_logic_unsigned.all;

ENTITY Controler_7segm IS
  PORT (
    clk        : IN  std_logic;                   
    S0         : IN  std_logic_vector(3 DOWNTO 0);
    S1         : IN  std_logic_vector(3 DOWNTO 0);
    S2         : IN  std_logic_vector(3 DOWNTO 0);
    anod       : OUT std_logic_vector(2 DOWNTO 0);
    catod      : OUT std_logic_vector(6 DOWNTO 0)
    );
END Controler_7segm;

ARCHITECTURE arch OF Controler_7segm IS

signal tmp: std_logic_vector(15 DOWNTO 0);
signal nr: std_logic_vector(3 DOWNTO 0);
BEGIN


process(clk)
begin
	if (rising_edge(clk)) then tmp <= tmp + 1;
	end if;
end process;



	catod<=not "0000001" when nr=x"0" else
	   not "1001111" when nr=x"1" else
	    not "0010010" when nr=x"2" else
	    not "0000110" when nr=x"3" else
	    not "1001100"when nr=x"4" else
	    not "0100100"when nr=x"5" else
	    not "0100000"when nr=x"6" else
	    not "0001111"when nr=x"7" else
	    not "0000000"when nr=x"8" else
	    not "0000100"when nr=x"9" else
	    not "0001000" when nr=x"a" else
	    not "1100000" when nr=x"b" else
	    not "0110001" when nr=x"c" else
	    not "1000010" when nr=x"d" else
	    not "0110000" when nr=x"e" else
	    not "0111000" when nr=x"f" else
	    not "1111111";



process(tmp)
begin
case(tmp(15 DOWNTO 14)) is --ia cele mai imp 2
	when "00" => anod <=not "1110";
	when "01" => anod <=not "1101";
	when "10" => anod <=not "1011";
	when others => anod <=not "ZZZZ";
end case;
end process;

process(tmp, S0, S1, S2)
begin
case(tmp(15 DOWNTO 14)) is
	when "00" => nr <= S0;
	when "01" => nr <= S1;
	when "10" => nr <= S2;
	when others => nr<="ZZZZ";
end case;
end process;	

END arch;

// VHDL entity debouncer, as the project stores it:
LIBRARY ieee;
USE ieee.std_logic_1164.all;
 
ENTITY debouncer IS
  PORT (btn: in std_logic;
  	R: in std_logic;
  	CLK: in std_logic;
  	btndb: out std_logic
    );
END debouncer;
 
ARCHITECTURE arh of debouncer is
signal t:std_logic_vector(2 downto 0);
component bistD is
port (D:in std_logic;
  	R:in std_logic;
  	CLK:in std_logic;
  	Q:out std_logic
    );
end component;
 
begin
D1: bistD port map(btn,R,CLK,t(0));
D2: bistD port map(t(0),R,CLK,t(1));
D3: bistD port map(t(1),R,CLK,t(2));
btndb<=t(0)and t(1) and (not t(2));
end arh;
 
LIBRARY ieee;
USE ieee.std_logic_1164.all;
 
ENTITY bistD IS
  PORT (
	D:in std_logic;
  	R:in std_logic;
  	CLK:in std_logic;
  	Q:out std_logic
    );
END bistD;
 
ARCHITECTURE arch OF bistD IS
 
BEGIN
process(CLK,R)
begin
	if(CLK='1' and CLK'EVENT) then
		if(R='1') then
			Q<='0';
		else
			Q<=D;
		end if;
	end if;
end process;
END arch;

// VHDL entity sau, as the project stores it:
LIBRARY ieee;
USE ieee.std_logic_1164.all;

ENTITY sau IS
  PORT (
   A,B: IN  std_logic;  
   C: OUT std_logic
    );
END sau;

ARCHITECTURE arch OF sau IS

BEGIN

 	C <= A or B;
END arch;
